# Fritzing sketch TouchMe (saved by Fritzing 0.9.0b)
circuit board: 8.46667cm x 5.64444cm
breadboards: 4

parts:
  Part1 = Arduino Uno (Rev3)
  LED1 = LED - 5mm [color="White (4500K)" package="5 mm [THT]"]
  LED2 = LED - 5mm [color="Green (570nm)" package="5 mm [THT]"]
  LED3 = LED - 5mm [color="Yellow (595nm)" package="5 mm [THT]"]
  LED4 = LED - 5mm [color="Red (633nm)" package="5 mm [THT]"]
  S1 = Pushbutton [package="[THT]"]
  S2 = Pushbutton [package="[THT]"]
  S3 = Pushbutton [package="[THT]"]
  S4 = Pushbutton [package="[THT]"]
  S5 = Pushbutton [package="[THT]"]
  J1 = Piezo Speaker
  7_Segment1 = 7 Segment Display
  U5 = 74HC595 [package="DIP16 [THT]"]
  LED5 = LED - 5mm [color="Red (633nm)" package="5 mm [THT]"]
  LED6 = LED - 5mm [color="Green (570nm)" package="5 mm [THT]"]
  R5 = Resistor [tolerance=±5% resistance=220 package=THT]
  R6 = Resistor [tolerance=±5% resistance=220 package=THT]
  R7 = Resistor [tolerance=±5% resistance=220 package=THT]
  R8 = Resistor [tolerance=±5% resistance=220 package=THT]
  R19 = Resistor [tolerance=±5% resistance=220 package=THT]
  R20 = Resistor [tolerance=±5% resistance=220 package=THT]
  R21 = Resistor [tolerance=±5% resistance=220 package=THT]
  Part2 = Arduino Uno (Rev3)
  LED7 = LED - 5mm [color="White (4500K)" package="5 mm [THT]"]
  LED8 = LED - 5mm [color="Green (570nm)" package="5 mm [THT]"]
  LED9 = LED - 5mm [color="Yellow (595nm)" package="5 mm [THT]"]
  LED10 = LED - 5mm [color="Red (633nm)" package="5 mm [THT]"]
  S6 = Pushbutton [package="[THT]"]
  S7 = Pushbutton [package="[THT]"]
  U6 = 74HC595 [package="DIP16 [THT]"]
  S8 = Pushbutton [package="[THT]"]
  S9 = Pushbutton [package="[THT]"]
  S10 = Pushbutton [package="[THT]"]
  J2 = Piezo Speaker
  7_Segment2 = 7 Segment Display
  IC2 = Hex Inverter Schmitt Trigger SN74HC14 [package="DIP (Dual Inline)"]  # not connected
  LED11 = LED - 5mm [color="Red (633nm)" package="5 mm [THT]"]
  LED12 = LED - 5mm [color="Green (570nm)" package="5 mm [THT]"]
  R27 = Resistor [tolerance=±5% resistance=220 package=THT]
  R28 = Resistor [tolerance=±5% resistance=220 package=THT]
  R29 = Resistor [tolerance=±5% resistance=220 package=THT]
  R30 = Resistor [tolerance=±5% resistance=220 package=THT]
  R31 = Resistor [tolerance=±5% resistance=220 package=THT]
  R32 = Resistor [tolerance=±5% resistance=220 package=THT]
  R33 = Resistor [tolerance=±5% resistance=220 package=THT]
  R34 = Resistor [tolerance=±5% resistance=220 package=THT]
  R35 = Resistor [tolerance=±5% resistance=220 package=THT]
  R36 = Resistor [tolerance=±5% resistance=220 package=THT]
  R37 = Resistor [tolerance=±5% resistance=220 package=THT]
  R38 = Resistor [tolerance=±5% resistance=220 package=THT]
  R39 = Resistor [tolerance=±5% resistance=220 package=THT]

nets:
  N1: Part1.A0, U5.SH_CP
  N2: Part1.A1, U5.ST_CP
  N3: Part1.A2, U5.DS
  N4: Part1.A3, LED5.anode
  N5: Part1.A4/SDA, LED6.anode
  N6: Part1.D8, S3.Pin_1, S3.Pin_2
  N7: Part1.D9_PWM, S4.Pin_1, S4.Pin_2
  N8: Part1.D10_PWM/SS, J1.pin2
  N9: Part1.D11_PWM/MOSI, S5.Pin_1, S5.Pin_2
  GND: Part1.GND, LED1.cathode, LED2.cathode, LED3.cathode, LED4.cathode, S1.Pin_3, S1.Pin_4, S2.Pin_3, S2.Pin_4, S3.Pin_3, S3.Pin_4, S4.Pin_3, S4.Pin_4, S5.Pin_3, S5.Pin_4, 7_Segment1.common_anode, U5.GND, U5.OE, R5.Pin_1, R6.Pin_0
  N10: Part1.D6_PWM, S1.Pin_1, S1.Pin_2
  N11: Part1.D7, S2.Pin_1, S2.Pin_2
  5V: Part1.5V, J1.pin1, U5.MR, U5.VCC
  N12: 7_Segment1.Segment_G, R19.Pin_0
  N13: 7_Segment1.Segment_F, R20.Pin_1
  N14: 7_Segment1.Segment_E, R21.Pin_0
  N15: 7_Segment1.Segment_D, R37.Pin_0
  N16: 7_Segment1.Segment_DP, R39.Pin_0
  N17: 7_Segment1.Segment_C, R38.Pin_0
  N18: 7_Segment1.Segment_B, R8.Pin_1
  N19: 7_Segment1.Segment_A, R7.Pin_1
  N20: U5.Q1, R7.Pin_0
  N21: U5.Q2, R8.Pin_0
  N22: U5.Q3, R19.Pin_1
  N23: U5.Q4, R20.Pin_0
  N24: U5.Q5, R21.Pin_1
  N25: U5.Q6, R39.Pin_1
  N26: U5.Q7, R38.Pin_1
  N27: U5.Q0, R37.Pin_1
  N28: LED5.cathode, R5.Pin_0
  N29: LED6.cathode, R6.Pin_1
  N30: Part2.A0, U6.SH_CP
  N31: Part2.A1, U6.ST_CP
  N32: Part2.A2, U6.DS
  N33: Part2.A3, LED11.anode
  N34: Part2.A4/SDA, LED12.anode
  N35: Part2.D8, S8.Pin_1, S8.Pin_2
  N36: Part2.D9_PWM, S9.Pin_1, S9.Pin_2
  N37: Part2.D10_PWM/SS, J2.pin2
  N38: Part2.D11_PWM/MOSI, S10.Pin_1, S10.Pin_2
  N39: Part2.GND, LED7.cathode, LED8.cathode, LED9.cathode, LED10.cathode, S6.Pin_3, S6.Pin_4, S7.Pin_3, S7.Pin_4, S8.Pin_3, S8.Pin_4, S9.Pin_3, S9.Pin_4
  N40: Part2.D6_PWM, S6.Pin_1, S6.Pin_2
  N41: Part2.D7, S7.Pin_1, S7.Pin_2
  N42: U6.Q1, R29.Pin_0
  N43: U6.Q2, R30.Pin_0
  N44: U6.Q3, R33.Pin_1
  N45: U6.Q4, R34.Pin_0
  N46: U6.Q5, R35.Pin_1
  N47: U6.Q6, R32.Pin_1
  N48: U6.Q7, R31.Pin_1
  N49: U6.GND, R27.Pin_0, R28.Pin_1, R34.Pin_1
  N50: U6.Q0, R36.Pin_1
  N51: S10.Pin_3, S10.Pin_4
  N52: 7_Segment2.Segment_G, 7_Segment2.Segment_F, R29.Pin_1
  N53: 7_Segment2.Segment_D, R33.Pin_0
  N54: 7_Segment2.Segment_DP, R36.Pin_0
  N55: 7_Segment2.Segment_B, 7_Segment2.Segment_A, R32.Pin_0
  N56: LED11.cathode, R28.Pin_0
  N57: LED12.cathode, R27.Pin_1
